# Fritzing sketch Quadcopter_6050 (saved by Fritzing 0.9.2b)
circuit board: 6.88566cm x 5.36311cm
breadboards: 1

parts:
  J1 = Basic Servo
  J2 = Basic Servo
  J3 = Basic Servo
  J4 = Basic Servo
  Quadcopter = Arduino Uno (Rev3)
  GY2 = MPU-6050 Board GY-521 [form="♀ (female)" package=THT]

nets:
  GND: J1.gnd, J2.gnd, J3.gnd, J4.gnd, Quadcopter.GND, GY2.pin2
  N1: J1.pulse, Quadcopter.D6_PWM
  N2: J2.pulse, Quadcopter.D9_PWM
  N3: J3.pulse, Quadcopter.D10_PWM/SS
  N4: J4.pulse, Quadcopter.D11_PWM/MOSI
  N5: Quadcopter.A4/SDA, GY2.pin4
  N6: Quadcopter.A5/SCL, GY2.pin3
  N7: Quadcopter.D2, GY2.pin8
  N8: Quadcopter.3V3, GY2.pin1

notes:
  Amir Aliabadi

custom parts:
  MPU-6050 Board GY-521: Acelerometro y Giroscopio MPU-6050 Board GY-521
